// Logisim project simulation.circ as structural Verilog: 4 circuits, main circuit Clock
module main (
  input  nIOA,
  input  nHOLD,
  input  nACK,
  output nMEM,
  output nIO,
  output E,
  output Q,
  output nVA,
  output nINT
);

  nand nand_1 (nMEM, nIOA, ~nVA);  // NAND_Gate
  nand nand_2 (nIO, ~nIOA, ~nVA);  // NAND_Gate
  Clock clock_1 (.nHOLD(nHOLD), .nIO(nIO), .nACK(nACK), .E(E), .Q(Q), .nVA(nVA), .nINT(nINT));
endmodule

// Clk
module Clock (
  input  nHOLD,
  input  nIO,
  input  nACK,
  output E,
  output Q,
  output nVA,
  output nINT
);

  wire nand_1_out, oscillator_1_cke, oscillator_1_ckq, rs_nand_1_q;

  Oscillator oscillator_1 (.nHOLD(nHOLD), .CKE(oscillator_1_cke), .CKQ(oscillator_1_ckq));
  nand nand_1 (nand_1_out, oscillator_1_cke, ~oscillator_1_ckq, ~nIO);  // NAND_Gate
  RS_NAND rs_nand_1 (.nS(nand_1_out), .nR(nACK), .Q(rs_nand_1_q), .nQ(nINT));
  or or_1 (E, oscillator_1_cke, rs_nand_1_q);
  and and_1 (Q, nINT, oscillator_1_ckq);
  nor nor_1 (nVA, E, Q);
endmodule

// Osc
module Oscillator (
  input  nHOLD,
  output CKE,
  output CKQ
);

  wire _4_x_fo_out, j_k_ff_1_qn, j_k_ff_2_qn, not_1_out;

  Clock_part _4_x_fo (.out(_4_x_fo_out));
  not not_1 (not_1_out, nHOLD);
  J_K_Flip_Flop j_k_ff_1 (
    .J(j_k_ff_2_qn), .clk(_4_x_fo_out), .K(CKE), .Q(CKQ), .Qn(j_k_ff_1_qn), .preset(1'b0), .en(1'b1),
    .reset(not_1_out));
  J_K_Flip_Flop j_k_ff_2 (
    .J(CKQ), .clk(_4_x_fo_out), .K(j_k_ff_1_qn), .Q(CKE), .Qn(j_k_ff_2_qn), .preset(1'b0), .en(1'b1),
    .reset(not_1_out));
endmodule

// RS
module RS_NAND (
  input  nS,
  input  nR,
  output Q,
  output nQ
);

  nand nand_1 (Q, nS, nQ);
  nand nand_2 (nQ, Q, nR);
endmodule
