// Digital circuit 7473.dig as structural Verilog
module _7473 (
  input  _1J,
  input  _1K,
  input  _1CP,
  input  _1R,
  input  _2J,
  input  _2K,
  input  _2CP,
  input  _2R,
  output _1Q,
  output _1Q_2,
  output _2Q,
  output _2Q_2
);

  wire not_1_out, not_2_out;

  not not_1 (not_1_out, _1R);
  not not_2 (not_2_out, _2R);
  JK_FF_AS jk_ff_as_1 (.Set(1'b0), .J(_1J), .C(_1CP), .K(_1K), .Clr(not_1_out), .Q(_1Q), .nQ(_1Q_2));
  JK_FF_AS jk_ff_as_2 (.Set(1'b0), .J(_2J), .C(_2CP), .K(_2K), .Clr(not_2_out), .Q(_2Q), .nQ(_2Q_2));

  // Notes on the sheet:
  //   _1J: pin 14
  //   _1K: pin 3
  //   _1CP: pin 1
  //   _1R: pin 2
  //   _1Q: pin 12
  //   _1Q_2: pin 13
  //   _2J: pin 7
  //   _2K: pin 10
  //   _2CP: pin 5
  //   _2R: pin 6
  //   _2Q: pin 9
  //   _2Q_2: pin 8
endmodule
