// Digital circuit ClockGenerator.dig as structural Verilog
module ClockGenerator (
  input  HOLD,
  input  IO,
  input  ACK,
  input  CLKx4,
  output VA,
  output INT,
  output Q,
  output E
);

  wire clockoscilator_1_e, clockoscilator_1_q, nand_1_out, or_1_out;

  ClockOscilator clockoscilator_1 (.HOLD(HOLD), .E(clockoscilator_1_e), .Q(clockoscilator_1_q), .CLKx4(CLKx4));
  nand nand_1 (nand_1_out, clockoscilator_1_e, ~clockoscilator_1_q, ~IO, ~VA);  // NAnd
  or or_1 (or_1_out, ~nand_1_out, ~INT);  // Or
  or or_2 (INT, ~or_1_out, ~ACK);  // Or
  or or_3 (E, clockoscilator_1_e, or_1_out);
  and and_1 (Q, INT, clockoscilator_1_q);
  nor nor_1 (VA, E, Q);

  // Notes on the sheet:
  //   HOLD: pin 2, default 1
  //   IO: pin 3, default 1
  //   ACK: pin 4
  //   VA: pin 6
  //   INT: pin 5
  //   Q: pin 7
  //   E: pin 8
  //   CLKx4: pin 1
endmodule
