// Digital circuit ClockOscilator.dig as structural Verilog
// Clock Generator for 6x09E
module ClockOscilator (
  input  HOLD,
  input  CLKx4,
  output E,
  output Q
);

  wire jk_ff_as_1_nq, jk_ff_as_2_nq, not_1_out;

  not not_1 (not_1_out, HOLD);
  JK_FF_AS jk_ff_as_1 (.Set(1'b0), .J(jk_ff_as_2_nq), .C(CLKx4), .K(E), .Clr(not_1_out), .Q(Q), .nQ(jk_ff_as_1_nq));
  JK_FF_AS jk_ff_as_2 (.Set(not_1_out), .J(Q), .C(CLKx4), .K(jk_ff_as_1_nq), .Clr(1'b0), .Q(E), .nQ(jk_ff_as_2_nq));

  // Notes on the sheet:
  //   HOLD: When asserted to 0, hold outputs as E=1 and Q=0., pin 2, default 1
  //   E: Clock output. Holding as 1 if #HOLD is 0., pin 4
  //   Q: Clock Q leading clock E by one-quater cycle. Holding as 0 if #HOLD is 0., pin 3
  //   CLKx4: pin 1
endmodule
