// Digital circuit ClockGenerator.dig as structural Verilog
module ClockGenerator (
  input  HOLD,
  input  IO,
  input  ACK,
  input  CLKx4,
  output VA,
  output INT,
  output Q,
  output E
);

  wire and_1_out, and_2_out, clockoscilator_1_p3, clockoscilator_1_p4, clockoscilator_1_p5, nand_1_out,
       or_1_out;

  // ClockOscilator clockoscilator_1: pin names not known; wires that end beside it: CLKx4, HOLD, clockoscilator_1_p3, clockoscilator_1_p4, clockoscilator_1_p5
  and and_1 (and_1_out, ~clockoscilator_1_p4, ~clockoscilator_1_p5);  // And
  and and_2 (and_2_out, ~IO, ~VA);  // And
  nand nand_1 (nand_1_out, and_1_out, and_2_out);
  or or_1 (or_1_out, ~nand_1_out, ~INT);  // Or
  or or_2 (INT, ~or_1_out, ~ACK);  // Or
  and and_3 (Q, ~clockoscilator_1_p3, ~or_1_out);  // And
  or or_3 (E, ~INT, ~clockoscilator_1_p5);  // Or
  nor nor_1 (VA, Q, E);

  // Notes on the sheet:
  //   HOLD: pin 2, default 1
  //   IO: pin 3, default 1
  //   ACK: pin 4, default 1
  //   VA: pin 6
  //   INT: pin 5
  //   Q: pin 7
  //   E: pin 8
  //   CLKx4: pin 1
endmodule
