// Digital circuit ClockOscilator.dig as structural Verilog
// Clock Generator for 6x09E
module ClockOscilator (
  input  CLKx4,
  input  HOLD,
  output E,
  output E_2,
  output Q,
  output Q_2
);

  // _7473 _7473_1: pin names not known; wires that end beside it: E_2, E, CLKx4, HOLD, Q, Q_2, CLKx4, HOLD, Q, Q_2, E, E_2

  // Notes on the sheet:
  //   CLKx4: pin 2
  //   E: Clock output. Holding as 1 if #HOLD is 0., pin 5
  //   E_2: pin 6
  //   HOLD: When asserted to 0, hold outputs as E=1 and Q=0., pin 3, default 1
  //   Q: pin 7
  //   Q_2: Clock Q leading clock E by one-quater cycle. Holding as 0 if #HOLD is 0., pin 8
endmodule
